// Logisim project prelab4drawing.circ as structural Verilog: 1 circuit, main circuit main
module main (
);

  wire discovery_p2_connector_1_p1, discovery_p2_connector_1_p2, discovery_p2_connector_1_p3,
       discovery_p2_connector_1_p4, discovery_p2_connector_1_p5, discovery_p2_connector_1_p6,
       pull_resistor_4_node, sn74hc541n_1_p1, sn74hc541n_1_p2, sn74hc541n_1_p11, sn74hc541n_1_p12,
       sn74hc541n_2_p1, sn74hc541n_2_p2, sn74hc541n_2_p3, sn74hc541n_2_p4, sn74hc541n_2_p7, sn74hc541n_2_p10,
       sn74hc541n_3_p1, sn74hc541n_3_p2, sn74hc541n_3_p3, sn74hc541n_3_p6;

  // Discovery_P2_Connector discovery_p2_connector_1: pin names not known; wires that end beside it: discovery_p2_connector_1_p1, discovery_p2_connector_1_p2, discovery_p2_connector_1_p3, discovery_p2_connector_1_p4, discovery_p2_connector_1_p5, discovery_p2_connector_1_p6
  // SN74HC541N sn74hc541n_1: pin names not known; wires that end beside it: sn74hc541n_1_p1, sn74hc541n_1_p2, discovery_p2_connector_1_p3, discovery_p2_connector_1_p6, discovery_p2_connector_1_p2, discovery_p2_connector_1_p5, discovery_p2_connector_1_p1, discovery_p2_connector_1_p4, 1'b0, 1'b1, sn74hc541n_1_p11, sn74hc541n_1_p12, sn74hc541n_1_p12, sn74hc541n_1_p12, sn74hc541n_1_p12, sn74hc541n_1_p12, sn74hc541n_1_p12, sn74hc541n_1_p12, sn74hc541n_1_p12, 1'b0, sn74hc541n_1_p12, sn74hc541n_1_p12
  // SN74HC541N sn74hc541n_2: pin names not known; wires that end beside it: sn74hc541n_2_p1, sn74hc541n_2_p2, sn74hc541n_2_p3, sn74hc541n_2_p4, sn74hc541n_2_p3, sn74hc541n_2_p2, sn74hc541n_2_p7, 1'b0, 1'b1, sn74hc541n_2_p10, sn74hc541n_2_p10, sn74hc541n_2_p10, sn74hc541n_2_p10, sn74hc541n_2_p10, sn74hc541n_2_p10, sn74hc541n_2_p10, sn74hc541n_2_p10, 1'b0, 1'b0, sn74hc541n_2_p10, sn74hc541n_2_p10
  // SN74HC541N sn74hc541n_3: pin names not known; wires that end beside it: sn74hc541n_3_p1, sn74hc541n_3_p2, sn74hc541n_3_p3, 1'b0, 1'b1, sn74hc541n_3_p6, sn74hc541n_3_p6, sn74hc541n_3_p6, sn74hc541n_3_p6, sn74hc541n_3_p6, sn74hc541n_3_p6, sn74hc541n_3_p6, sn74hc541n_3_p6, 1'b0, sn74hc541n_3_p6, sn74hc541n_3_p6, sn74hc541n_3_p6
  Pull_Resistor pull_resistor_1 (.node(sn74hc541n_1_p12));
  Pull_Resistor pull_resistor_2 (.node(sn74hc541n_2_p10));
  Pull_Resistor pull_resistor_3 (.node(sn74hc541n_3_p6));
  // DIP_Switch dip_switch_1: pin names not known; wires that end beside it: 1'b0, sn74hc541n_1_p12, sn74hc541n_1_p12, sn74hc541n_1_p12, sn74hc541n_1_p12, sn74hc541n_1_p12, sn74hc541n_1_p12, 1'b1, 1'b1, 1'b1, 1'b1, 1'b1, 1'b1
  // DIP_Switch dip_switch_2: pin names not known; wires that end beside it: 1'b0, sn74hc541n_2_p10, sn74hc541n_2_p10, sn74hc541n_2_p10, sn74hc541n_2_p10, sn74hc541n_2_p10, sn74hc541n_2_p10, 1'b1, 1'b1, 1'b1, 1'b1, 1'b1, 1'b1, 1'b1, 1'b1
  // DIP_Switch dip_switch_3: pin names not known; wires that end beside it: sn74hc541n_3_p6, sn74hc541n_3_p6, sn74hc541n_3_p6, sn74hc541n_3_p6, sn74hc541n_3_p6, 1'b1, 1'b1, 1'b1, 1'b1, 1'b1, 1'b1, 1'b1, 1'b1, 1'b1, 1'b1
  Pull_Resistor #(.pull(1)) pull_resistor_4 (.node(pull_resistor_4_node));
  // BarGraph_LED bargraph_led_1: pin names not known; wires that end beside it: pull_resistor_4_node, pull_resistor_4_node, 1'b0, 1'b0, 1'b0, 1'b0, 1'b0, 1'b0, 1'b0, 1'b0, 1'b0, 1'b0

  // Notes on the sheet:
  //   Input A
  //   Inpuut B
  //   Other Inputs
  //   outputs
endmodule
