// Logisim project prelab7_schematic.circ as structural Verilog: 1 circuit, main circuit main
module main (
);

  wire JC1, JC2, JC3, JC4, JC7, JC8, JC10, nand_2_out, pull_resistor_1_node, R_cmd, sn74hc540n_1_p9;

  Pull_Resistor #(.pull(1)) pull_resistor_1 (.node(pull_resistor_1_node));
  Pull_Resistor pull_resistor_2 (.node(R_cmd));
  nand nand_1 (JC10, nand_2_out, pull_resistor_1_node);
  nand nand_2 (nand_2_out, JC10, pull_resistor_1_node);
  // DIP_Switch dip_switch_1: pin names not known; wires that end beside it: R_cmd, R_cmd, R_cmd, R_cmd, R_cmd, R_cmd, R_cmd, R_cmd, 1'b1, 1'b1, 1'b1, 1'b1, 1'b1, 1'b1, 1'b1, 1'b1
  // SN74HC540N sn74hc540n_1: pin names not known; wires that end beside it: JC2, 1'b0, JC4, JC7, JC8, JC1, 1'b1, 1'b0, sn74hc540n_1_p9, sn74hc540n_1_p9, sn74hc540n_1_p9, R_cmd, R_cmd
  // SN74HC541N sn74hc541n_1: pin names not known; wires that end beside it: 1'b0, 1'b0, JC3, 1'b1, 1'b0, sn74hc540n_1_p9, sn74hc540n_1_p9
  Pull_Resistor pull_resistor_3 (.node(sn74hc540n_1_p9));
  // BarGraph_LED bargraph_led_1: pin names not known; wires that end beside it: sn74hc540n_1_p9, sn74hc540n_1_p9, sn74hc540n_1_p9, sn74hc540n_1_p9, sn74hc540n_1_p9, sn74hc540n_1_p9, sn74hc540n_1_p9, sn74hc540n_1_p9, sn74hc540n_1_p9, 1'b1, 1'b1, 1'b1, 1'b1, 1'b1, 1'b1, 1'b1, 1'b1

  // Other names for the same wires on the sheet: W_cmd = R_cmd

  // Notes on the sheet:
  //   3-prong switch
  //   Bounce Free Clock
endmodule
