// Logisim project Prelab_10schematic.circ as structural Verilog: 1 circuit, main circuit main
module main (
);

  wire JB1, JB2, JB7, JB8, JB9, JB10, nand_2_out, nand_4_out, pull_resistor_1_node, pull_resistor_3_node,
       sn74hc540n_1_p9;

  Pull_Resistor #(.pull(1)) pull_resistor_1 (.node(pull_resistor_1_node));
  nand nand_1 (JB1, nand_2_out, pull_resistor_1_node);
  nand nand_2 (nand_2_out, JB1, pull_resistor_1_node);
  // SN74HC540N sn74hc540n_1: pin names not known; wires that end beside it: 1'b0, JB7, JB8, JB9, JB10, 1'b0, 1'b1, 1'b0, sn74hc540n_1_p9, sn74hc540n_1_p9, sn74hc540n_1_p9, sn74hc540n_1_p9
  Pull_Resistor pull_resistor_2 (.node(sn74hc540n_1_p9));
  Pull_Resistor #(.pull(1)) pull_resistor_3 (.node(pull_resistor_3_node));
  nand nand_3 (JB2, nand_4_out, pull_resistor_3_node);
  nand nand_4 (nand_4_out, JB2, pull_resistor_3_node);
  // BarGraph_LED bargraph_led_1: pin names not known; wires that end beside it: sn74hc540n_1_p9, sn74hc540n_1_p9, sn74hc540n_1_p9, sn74hc540n_1_p9, sn74hc540n_1_p9, sn74hc540n_1_p9, sn74hc540n_1_p9, sn74hc540n_1_p9, sn74hc540n_1_p9, sn74hc540n_1_p9, 1'b1, 1'b1, 1'b1, 1'b1, 1'b1, 1'b1, 1'b1, 1'b1

  // Notes on the sheet:
  //   3-prong switch
  //   X1
  //   3-prong switch
  //   X2
endmodule
