// Logisim project Prelab_8_schematic.circ as structural Verilog: 1 circuit, main circuit main
module main (
);

  wire A10, JA1, JA2, JA3, JA4, JA7, JA8, JA9, JA10, JB1, JB2, JB3, JB4, JB7, JB8, JB9, JB10, JC1, JC2,
       nand_2_out, pull_resistor_1_node, sn74hc540n_1_p11, sn74hc541n_1_p11, sn74hc541n_2_p7;

  Pull_Resistor #(.pull(1)) pull_resistor_1 (.node(pull_resistor_1_node));
  // SN74HC541N sn74hc541n_1: pin names not known; wires that end beside it: JB1, JB2, JB4, JB7, JB8, JB9, JB10, A10, 1'b0, 1'b1, sn74hc541n_1_p11, sn74hc541n_1_p11, sn74hc541n_1_p11, sn74hc541n_1_p11, sn74hc541n_1_p11, sn74hc541n_1_p11, sn74hc541n_1_p11, sn74hc541n_1_p11, 1'b0, sn74hc541n_1_p11, sn74hc541n_1_p11, sn74hc541n_1_p11
  // SN74HC540N sn74hc540n_1: pin names not known; wires that end beside it: 1'b0, JA7, JA8, JA9, JA10, JC1, JC2, 1'b0, 1'b1, 1'b0, sn74hc540n_1_p11, sn74hc540n_1_p11, sn74hc540n_1_p11, sn74hc540n_1_p11, sn74hc540n_1_p11, sn74hc540n_1_p11, sn74hc540n_1_p11, sn74hc540n_1_p11
  nand nand_1 (JB3, nand_2_out, pull_resistor_1_node);
  nand nand_2 (nand_2_out, JB3, pull_resistor_1_node);
  Pull_Resistor pull_resistor_2 (.node(sn74hc541n_1_p11));
  Pull_Resistor #(.pull(1)) pull_resistor_3 (.node(sn74hc540n_1_p11));
  // DIP_Switch dip_switch_1: pin names not known; wires that end beside it: 1'b0, sn74hc541n_1_p11, sn74hc541n_1_p11, sn74hc541n_1_p11, sn74hc541n_1_p11, sn74hc541n_1_p11, 1'b1, 1'b1, 1'b1, 1'b1, 1'b1, 1'b1, 1'b1
  // BarGraph_LED bargraph_led_1: pin names not known; wires that end beside it: sn74hc540n_1_p11, sn74hc540n_1_p11, sn74hc540n_1_p11, sn74hc540n_1_p11, sn74hc540n_1_p11, sn74hc540n_1_p11, sn74hc540n_1_p11, sn74hc540n_1_p11, 1'b0, 1'b0, 1'b0, 1'b0, 1'b0, 1'b0, 1'b0, 1'b0, 1'b0, 1'b0, 1'b1
  // SN74HC541N sn74hc541n_2: pin names not known; wires that end beside it: JA1, JA2, JA3, JA4, 1'b0, 1'b1, sn74hc541n_2_p7, sn74hc541n_2_p7, sn74hc541n_2_p7, sn74hc541n_2_p7, sn74hc541n_2_p7, sn74hc541n_2_p7, sn74hc541n_2_p7, sn74hc541n_2_p7, 1'b0, sn74hc541n_2_p7, sn74hc541n_2_p7
  Pull_Resistor pull_resistor_4 (.node(sn74hc541n_2_p7));
  // DIP_Switch dip_switch_2: pin names not known; wires that end beside it: 1'b0, sn74hc541n_2_p7, sn74hc541n_2_p7, sn74hc541n_2_p7, sn74hc541n_2_p7, sn74hc541n_2_p7, sn74hc541n_2_p7, 1'b1, 1'b1, 1'b1, 1'b1, 1'b1, 1'b1, 1'b1, 1'b1

  // Notes on the sheet:
  //   3-prong switch
  //   Bounce Free Clock
endmodule
